// Logisim project PROJECT.circ as structural Verilog: 7 circuits, main circuit main
module main (
);

  wire BTN_DOWN, BTN_LEFT, BTN_RES, BTN_RIGHT, BTN_UP, DOWN_out, EV_BONUS_PICKUP, EV_EXIT_REACHED,
       EV_KEY_PICKUP, EV_PLAYER_MOVE, EV_TRAP_TRIGGER, LEFT_out, LOAD_X, LOAD_Y, RESET, RIGHT_out, TACTS,
       UP_out, WE_MAP;
  wire [3:0] CELL_TYPE, SCAN_Q;
  wire [5:0] NEW_X, NEW_Y, POS_X, POS_Y;
  wire [11:0] ADDR, ADDR_NEXT;

  Clock clock_1 (.out(TACTS));
  Button RIGHT (.out(RIGHT_out));
  Button LEFT (.out(LEFT_out));
  Button UP (.out(UP_out));
  Button DOWN (.out(DOWN_out));
  Button u_RESET (.out(RESET));
  BTN_INPUT btn_input_1 (
    .TACT(TACTS), .RIGHT(RIGHT_out), .LEFT(LEFT_out), .UP(UP_out), .DOWN(DOWN_out), .RESET(RESET),
    .B_RIGHT(BTN_RIGHT), .B_LEFT(BTN_LEFT), .B_UP(BTN_UP), .B_DOWN(BTN_DOWN), .B_RESET(BTN_RES));
  MOVE_LOGIC move_logic_1 (
    .POS_Y(POS_Y), .POS_X(POS_X), .CELL_TYPE(CELL_TYPE), .MOVE_ENABLE(1'b1), .GAME_STATE(2'b00),
    .B_RIGHT(BTN_RIGHT), .B_LEFT(BTN_LEFT), .EXIT_OPEN(1'b0), .B_UP(BTN_UP), .B_DOWN(BTN_DOWN),
    .ADDR_NEXT(ADDR_NEXT), .NEW_X(NEW_X), .NEW_Y(NEW_Y), .EV_KEY_PICKUP(EV_KEY_PICKUP),
    .EV_TRAP_TRIGGER(EV_TRAP_TRIGGER), .EV_BONUS_PICKUP(EV_BONUS_PICKUP), .LOAD_X(LOAD_X),
    .EV_EXIT_REACHED(EV_EXIT_REACHED), .EV_PLAYER_MOVE(EV_PLAYER_MOVE), .LOAD_Y(LOAD_Y), .WE_MAP(WE_MAP));
  DotMatrix #(.inputtype("row"), .matrixcols(32), .matrixrows(32)) dotmatrix_1 ();  // open: row0, row1, row2, row3, row4, row5, row6, row7, row8, row9, row10, row11, row12, row13, row14, row15, row16, row17, row18, row19, row20, row21, row22, row23, row24, row25, row26, row27, row28, row29, row30, row31
  PLAYER_POS player_pos_1 (
    .NEW_X(NEW_X), .NEW_Y(NEW_Y), .LOAD_X(LOAD_X), .RESET_3(RESET), .LOAD_Y(LOAD_Y), .POS_X(POS_X),
    .RESET(BTN_RES), .RESET_2(BTN_RES), .TACT(TACTS), .TACT_2(TACTS), .POS_Y(POS_Y), .ADDR(ADDR));
  MAP_MEM map_mem_1 (.ADDR(ADDR), .WE(WE_MAP), .TACT(TACTS), .SCAN_Q(SCAN_Q), .CELL_TYPE(CELL_TYPE));
endmodule

module BTN_INPUT (
  input  TACT,
  input  RIGHT,
  input  LEFT,
  input  UP,
  input  DOWN,
  input  RESET,
  output B_RIGHT,
  output B_LEFT,
  output B_UP,
  output B_DOWN,
  output B_RESET
);

  wire d_ff_1_q, d_ff_2_q, d_ff_3_q, d_ff_4_q, not_1_out, not_2_out, not_3_out, not_4_out;

  D_Flip_Flop d_ff_1 (.clk(TACT), .D(RIGHT), .Q(d_ff_1_q));  // open: Qn, preset, en, reset
  D_Flip_Flop d_ff_2 (.clk(TACT), .D(LEFT), .Q(d_ff_2_q));  // open: Qn, preset, en, reset
  D_Flip_Flop d_ff_3 (.clk(TACT), .D(UP), .Q(d_ff_3_q));  // open: Qn, preset, en, reset
  D_Flip_Flop d_ff_4 (.clk(TACT), .D(DOWN), .Q(d_ff_4_q));  // open: Qn, preset, en, reset
  not not_1 (not_1_out, d_ff_1_q);
  not not_2 (not_2_out, d_ff_2_q);
  not not_3 (not_3_out, d_ff_3_q);
  not not_4 (not_4_out, d_ff_4_q);
  and and_1 (B_RIGHT, not_1_out, RIGHT);
  and and_2 (B_LEFT, not_2_out, LEFT);
  and and_3 (B_UP, not_3_out, UP);
  and and_4 (B_DOWN, not_4_out, DOWN);

  assign B_RESET = RESET;
endmodule

module PLAYER_POS (
  input  [5:0] NEW_X,
  input  RESET,
  input  TACT,
  input  [5:0] NEW_Y,
  input  RESET_2,
  input  TACT_2,
  input  LOAD_X,
  input  RESET_3,
  input  LOAD_Y,
  output [5:0] POS_X,
  output [11:0] ADDR,
  output [5:0] POS_Y
);

  wire LOAD_X_OR_RESET, LOAD_Y_OR_RESET;
  wire [5:0] multiplexer_1_out, multiplexer_2_out;

  or or_1 (LOAD_X_OR_RESET, LOAD_X, RESET_3);
  or or_2 (LOAD_Y_OR_RESET, RESET_3, LOAD_Y);
  Multiplexer #(.width(6), .enable("false")) multiplexer_1 (
    .in0(NEW_X), .in1(6'b000010), .out(multiplexer_1_out), .sel(RESET));
  Multiplexer #(.width(6), .enable("false")) multiplexer_2 (
    .in0(NEW_Y), .in1(6'b000010), .out(multiplexer_2_out), .sel(RESET_2));
  Register #(.width(6)) u_POS_X (.D(multiplexer_1_out), .en(LOAD_X_OR_RESET), .Q(ADDR[5:0]), .clk(TACT));  // open: clr
  Register #(.width(6)) u_POS_Y (
    .D(multiplexer_2_out), .en(LOAD_Y_OR_RESET), .Q(ADDR[11:6]), .clk(TACT_2));  // open: clr

  assign POS_X = ADDR[5:0];
  assign POS_Y = ADDR[11:6];

  // Notes on the sheet:
  //   START_X
  //   START_Y
endmodule

module MAP_MEM (
  input  [11:0] ADDR,
  input  WE,
  input  TACT,
  output [3:0] CELL_TYPE,
  output [3:0] SCAN_Q
);

  RAM #(.addrWidth(12), .dataWidth(4), .bus("separate")) ram_1 (
    .addr(ADDR), .din(4'b0000), .data(CELL_TYPE), .str(WE), .sel(1'b1), .clk(TACT), .ld(1'b1), .clr(1'b0));
  RAM #(.addrWidth(12), .dataWidth(4)) ram_2 ();  // open: addr, data, sel, clk, ld, clr
  Counter counter_1 ();  // open: load, D, count, Q, carry, clk, clr

  assign SCAN_Q = CELL_TYPE;

  // Notes on the sheet:
  //   MAP_DATA_BACKUP
  //   MAP_DATA
endmodule

module RESET (
  input  TACT
);
endmodule

module MOVE_LOGIC (
  input  [5:0] POS_Y,
  input  [5:0] POS_X,
  input  [3:0] CELL_TYPE,
  input  MOVE_ENABLE,
  input  [1:0] GAME_STATE,
  input  B_RIGHT,
  input  B_LEFT,
  input  EXIT_OPEN,
  input  B_UP,
  input  B_DOWN,
  output [11:0] ADDR_NEXT,
  output [5:0] NEW_X,
  output [5:0] NEW_Y,
  output EV_KEY_PICKUP,
  output EV_TRAP_TRIGGER,
  output EV_BONUS_PICKUP,
  output LOAD_X,
  output EV_EXIT_REACHED,
  output EV_PLAYER_MOVE,
  output LOAD_Y,
  output WE_MAP
);

  wire ALLOWED, and_10_out, CAN_ENTER, comparator_2_eq, comparator_3_gt, comparator_4_gt, comparator_5_eq,
       DO_D, DO_L, DO_R, DO_U, DOWN_OK, GANE_ACTIVE, IS_BONUS, IS_EXIT_C, IS_EXIT_O, IS_KEY, IS_PASS,
       IS_START, IS_TRAP, IS_WALL, LEFT_OK, not_1_out, or_8_out, RIGHT_OK, SAFE_D, SAFE_L, SAFE_R, SAFE_U,
       UP_OK;
  wire [1:0] or_4_out;
  wire [5:0] NEW_X_L, NEW_X_R, NEW_Y_D, NEW_Y_U;

  Decoder #(.select(4), .enable("false")) decoder_1 (
    .out0(IS_PASS), .out1(IS_WALL), .out2(IS_KEY), .out3(IS_EXIT_C), .out4(IS_EXIT_O), .out5(IS_TRAP),
    .out6(IS_BONUS), .out7(IS_START), .sel(CELL_TYPE));  // open: out8, out9, out10, out11, out12, out13, out14, out15
  Comparator #(.width(2)) comparator_1 (.a(GAME_STATE), .b(2'b00), .eq(GANE_ACTIVE));  // open: gt, lt
  Adder #(.width(6)) adder_1 (.a(POS_Y), .b(6'b000001), .out(NEW_Y_U));  // open: cin, cout
  Adder #(.width(6)) adder_2 (.a(POS_X), .b({6{1'b0}}), .out(NEW_X_R));  // open: cin, cout
  Subtractor #(.width(6)) subtractor_1 (.a(POS_Y), .b(6'b111110), .out(NEW_Y_D));  // open: bin, bout
  Subtractor #(.width(6)) subtractor_2 (.a(POS_X), .b({6{1'b0}}), .out(NEW_X_L));  // open: bin, bout
  Comparator #(.width(6), .mode("unsigned")) comparator_2 (
    .a(POS_Y), .b({6{1'b0}}), .eq(comparator_2_eq));  // open: gt, lt
  Comparator #(.width(6), .mode("unsigned")) comparator_3 (
    .a(NEW_X_R), .b(6'b111110), .gt(comparator_3_gt));  // open: eq, lt
  Comparator #(.width(6), .mode("unsigned")) comparator_4 (
    .a(NEW_Y_D), .b({6{1'b0}}), .gt(comparator_4_gt));  // open: eq, lt
  Comparator #(.width(6), .mode("unsigned")) comparator_5 (
    .a(POS_X), .b({6{1'b0}}), .eq(comparator_5_eq));  // open: gt, lt
  and and_1 (ALLOWED, GANE_ACTIVE, MOVE_ENABLE);
  and and_2 (RIGHT_OK, B_RIGHT, MOVE_ENABLE);
  and and_3 (LEFT_OK, B_LEFT, MOVE_ENABLE);
  and and_4 (UP_OK, B_UP, MOVE_ENABLE);
  and and_5 (DOWN_OK, B_DOWN, MOVE_ENABLE);
  not not_1 (not_1_out, comparator_5_eq);
  not not_2 (SAFE_U, comparator_2_eq);
  not not_3 (SAFE_R, comparator_3_gt);
  not not_4 (SAFE_D, comparator_4_gt);
  not not_5 (SAFE_L, not_1_out);
  or or_1 (CAN_ENTER, IS_PASS, IS_KEY, IS_EXIT_O, IS_TRAP, IS_BONUS, IS_START);
  Multiplexer #(.select(2), .width(12), .enable("false")) multiplexer_1 (
    .in0({POS_Y, NEW_X_R}), .in1({POS_Y, NEW_X_L}), .in2({NEW_Y_D, POS_X}), .in3({NEW_Y_U, POS_X}),
    .out(ADDR_NEXT), .sel(or_4_out));
  and and_6 (DO_R, RIGHT_OK, SAFE_R, CAN_ENTER);
  and and_7 (DO_L, LEFT_OK, SAFE_L, CAN_ENTER);
  and and_8 (DO_U, UP_OK, SAFE_U, CAN_ENTER);
  and and_9 (DO_D, DOWN_OK, SAFE_D, CAN_ENTER);
  or or_2 (LOAD_X, DO_R, DO_L);
  or or_3 (LOAD_Y, DO_U, DO_D);
  or or_4 (or_4_out[0], LEFT_OK, UP_OK);
  or or_5 (or_4_out[1], DOWN_OK, UP_OK);
  Multiplexer #(.width(6), .enable("false")) multiplexer_2 (.in0(NEW_X_R), .in1(NEW_X_L), .out(NEW_X), .sel(DO_L));
  Multiplexer #(.width(6), .enable("false")) multiplexer_3 (.in0(NEW_Y_D), .in1(NEW_Y_U), .out(NEW_Y), .sel(DO_U));
  and and_10 (and_10_out, IS_EXIT_C, EXIT_OPEN);
  or or_6 (WE_MAP, EV_KEY_PICKUP, EV_BONUS_PICKUP);
  or or_7 (EV_PLAYER_MOVE, DO_R, DO_L, DO_U, DO_D);
  and and_11 (EV_KEY_PICKUP, EV_PLAYER_MOVE, IS_KEY);
  and and_12 (EV_TRAP_TRIGGER, EV_PLAYER_MOVE, IS_TRAP);
  and and_13 (EV_BONUS_PICKUP, EV_PLAYER_MOVE, IS_BONUS);
  or or_8 (or_8_out, and_10_out, IS_EXIT_O);
  and and_14 (EV_EXIT_REACHED, EV_PLAYER_MOVE, or_8_out);
  BitSelector bitselector_1 ();  // open: in, out, sel

  // Other names for the same wires on the sheet: ANY_MOVE = EV_PLAYER_MOVE

  // Notes on the sheet:
  //   UP
  //   RIGHT
  //   DOWN
  //   LEFT
  //   RIGHT
  //   LEFT
  //   DOWN
  //   UP
  //   DO RLUD
endmodule

module DISPLAY (
  input  FINAL_PIXEL,
  input  FINAL_PIXEL_2,
  input  TACT,
  input  MAP_Q,
  input  POS_X,
  input  POS_Y,
  output SCAN_ADDR
);

  wire clock_1_out, SCAN_X_carry;

  Clock clock_1 (.out(clock_1_out));
  Counter #(.width(5), .max('h1e)) SCAN_X (.carry(SCAN_X_carry), .clk(clock_1_out));  // open: load, D, count, Q, clr
  Counter #(.width(5), .max('h1e)) SCAN_Y (.clk(SCAN_X_carry));  // open: load, D, count, Q, carry, clr
  Shift_Register #(.length(32)) shift_register_1 (
    .shift(FINAL_PIXEL), .in(FINAL_PIXEL_2), .clk(clock_1_out), .load(FINAL_PIXEL));  // open: out, clr, d0, q0, d1, q1, d2, q2, d3, q3, d4, q4, d5, q5, d6, q6, d7, q7, d8, q8, d9, q9, d10, q10, d11, q11, d12, q12, d13, q13, d14, q14, d15, q15, d16, q16, d17, q17, d18, q18, d19, q19, d20, q20, d21, q21, d22, q22, d23, q23, d24, q24, d25, q25, d26, q26, d27, q27, d28, q28, d29, q29, d30, q30, d31, q31
endmodule
